// Logisim project snake.circ as structural Verilog: 9 circuits, main circuit main
module main (
);

  wire clock_1_out, clock_2_out, clock_3_out, not_1_out;
  wire [3:0] bit_extender_3_out;
  wire [7:0] alu_1_out_4, bit_extender_1_out, bit_extender_2_out, multiplexer_1_out, pc_1_out_4, ram_1_data,
       registergroupv2_1_out_7, registergroupv2_1_out_8, registergroupv2_1_out_9, registergroupv2_1_out_10,
       registergroupv2_1_out_11, screendecoder_1_out_3, screendecoder_1_out_4, screendecoder_1_out_5,
       screendecoder_1_out_6, screendecoder_1_out_7, screendecoder_1_out_8, screendecoder_1_out_9,
       screendecoder_1_out_10;
  wire [31:0] rom_1_data;

  Bit_Extender #(.in_width(32), .out_width(8)) bit_extender_1 (.in(rom_1_data), .out(bit_extender_1_out));
  ROM #(.dataWidth(32)) rom_1 (.addr(pc_1_out_4), .data(rom_1_data));  // open: sel
  Clock clock_1 (.out(clock_1_out));
  PC pc_1 (.in_3(clock_1_out), .out_4(pc_1_out_4), .in_1(rom_1_data[28]), .in_2(bit_extender_1_out));
  Bit_Extender #(.in_width(10), .out_width(8)) bit_extender_2 (.in(rom_1_data[15:6]), .out(bit_extender_2_out));
  Bit_Extender #(.in_width(6), .out_width(4)) bit_extender_3 (.in(rom_1_data[5:0]), .out(bit_extender_3_out));
  RegisterGroupV2 registergroupv2_1 (
    .in_1(rom_1_data[25:21]), .in_3(multiplexer_1_out), .in_4(rom_1_data[20:16]), .in_5(rom_1_data[31]),
    .in_6(clock_2_out), .out_7(registergroupv2_1_out_7), .out_8(registergroupv2_1_out_8),
    .in_2(rom_1_data[20:16]), .out_9(registergroupv2_1_out_9), .out_10(registergroupv2_1_out_10),
    .out_11(registergroupv2_1_out_11));
  Clock clock_2 (.out(clock_2_out));
  ScreenDecoder screendecoder_1 (
    .out_3(screendecoder_1_out_3), .out_4(screendecoder_1_out_4), .out_5(screendecoder_1_out_5),
    .out_6(screendecoder_1_out_6), .out_7(screendecoder_1_out_7), .out_8(screendecoder_1_out_8),
    .out_9(screendecoder_1_out_9), .out_10(screendecoder_1_out_10), .in_2(registergroupv2_1_out_11),
    .in_1(registergroupv2_1_out_10));
  DotMatrix #(.matrixcols(8), .matrixrows(8)) dotmatrix_1 (
    .col0(screendecoder_1_out_3), .col1(screendecoder_1_out_4), .col2(screendecoder_1_out_5),
    .col3(screendecoder_1_out_6), .col4(screendecoder_1_out_7), .col5(screendecoder_1_out_8),
    .col6(screendecoder_1_out_9), .col7(screendecoder_1_out_10));
  Multiplexer #(.width(8)) multiplexer_1 (
    .in0(alu_1_out_4), .in1(ram_1_data), .out(multiplexer_1_out), .sel(rom_1_data[30]));  // open: en
  ALU alu_1 (.in_1(registergroupv2_1_out_7), .in_2(bit_extender_2_out), .out_4(alu_1_out_4), .in_3(bit_extender_3_out));
  not not_1 (not_1_out, rom_1_data[29]);
  Clock clock_3 (.out(clock_3_out));
  RAM #(.bus("separate")) ram_1 (
    .addr(alu_1_out_4), .din(registergroupv2_1_out_8), .data(ram_1_data), .str(rom_1_data[29]),
    .clk(clock_3_out), .ld(not_1_out));  // open: sel, clr

  // Notes on the sheet:
  //   contents of rom_1 (hex, n*v repeats v):
  //   80e00000 80e10080 20010040 20010080 c0060080 c0010040 80220040 20020040 80450000 10000005
endmodule

module AU (
  input  [7:0] in_1,
  input  [7:0] in_2,
  input  in_3,
  output [7:0] out_4
);

  wire [7:0] adder_1_out, subtractor_1_out;

  Adder adder_1 (.a(in_1), .b(in_2), .out(adder_1_out));  // open: cin, cout
  Subtractor subtractor_1 (.a(in_1), .b(in_2), .out(subtractor_1_out));  // open: bin, bout
  Multiplexer #(.width(8)) multiplexer_1 (
    .in0(adder_1_out), .in1(subtractor_1_out), .out(out_4), .sel(in_3));  // open: en
endmodule

module LU (
  input  [7:0] in_1,
  input  [7:0] in_2,
  input  in_3,
  output [7:0] out_4
);

  wire [7:0] and_1_out, or_1_out;

  assign and_1_out = in_1 & in_2;  // AND_Gate and_1, 8 bits wide
  assign or_1_out = in_1 | in_2;  // OR_Gate or_1, 8 bits wide
  Multiplexer #(.width(8)) multiplexer_1 (.in0(and_1_out), .in1(or_1_out), .out(out_4), .sel(in_3));  // open: en
endmodule

module ALU (
  input  [7:0] in_1,
  input  [7:0] in_2,
  input  [3:0] in_3,
  output [7:0] out_4
);

  wire [7:0] au_1_out_4, lu_1_out_4;

  AU au_1 (.in_1(in_1), .in_2(in_2), .in_3(in_3[2]), .out_4(au_1_out_4));
  LU lu_1 (.in_1(in_1), .in_2(in_2), .in_3(in_3[3]), .out_4(lu_1_out_4));
  Multiplexer #(.width(8)) multiplexer_1 (.in0(au_1_out_4), .in1(lu_1_out_4), .out(out_4), .sel(in_3[1]));  // open: en
endmodule

module RegistetGroup (
  input  [4:0] in_1,
  input  [7:0] in_2,
  input  [4:0] in_3,
  input  in_4,
  input  in_5,
  output [7:0] out_6
);

  wire and_1_out, and_2_out, and_3_out, and_4_out, and_5_out, and_6_out, and_7_out, decoder_1_out0,
       decoder_1_out1, decoder_1_out2, decoder_1_out3, decoder_1_out4, decoder_1_out5, decoder_1_out6,
       decoder_1_out7;
  wire [7:0] register_1_q, register_2_q, register_3_q, register_4_q, register_5_q, register_6_q,
       register_7_q, register_8_q;

  Decoder #(.select(3)) decoder_1 (
    .out0(decoder_1_out0), .out1(decoder_1_out1), .out2(decoder_1_out2), .out3(decoder_1_out3),
    .out4(decoder_1_out4), .out5(decoder_1_out5), .out6(decoder_1_out6), .out7(decoder_1_out7),
    .sel(in_3[2:0]));  // open: en
  and and_1 (and_1_out, in_4, decoder_1_out0);
  and and_2 (and_2_out, in_4, decoder_1_out1);
  and and_3 (and_3_out, in_4, decoder_1_out2);
  and and_4 (and_4_out, in_4, decoder_1_out3);
  and and_5 (and_5_out, in_4, decoder_1_out4);
  and and_6 (and_6_out, in_4, decoder_1_out5);
  and and_7 (and_7_out, in_4, decoder_1_out6);
  // AND_Gate and_8 has open pins: in0=in_4, in1=decoder_1_out7, out=open
  Register register_1 (.D(in_2), .en(and_1_out), .Q(register_1_q), .clk(in_5));  // open: clr
  Register register_2 (.D(in_2), .en(and_2_out), .Q(register_2_q), .clk(in_5));  // open: clr
  Register register_3 (.D(in_2), .en(and_3_out), .Q(register_3_q), .clk(in_5));  // open: clr
  Register register_4 (.D(in_2), .en(and_4_out), .Q(register_4_q), .clk(in_5));  // open: clr
  Register register_5 (.D(in_2), .en(and_5_out), .Q(register_5_q), .clk(in_5));  // open: clr
  Register register_6 (.D(in_2), .en(and_6_out), .Q(register_6_q), .clk(in_5));  // open: clr
  Register register_7 (.D(in_2), .en(and_7_out), .Q(register_7_q), .clk(in_5));  // open: clr
  Register register_8 (.Q(register_8_q), .clr(1'b1));  // open: D, en, clk
  Multiplexer #(.select(3), .width(8)) multiplexer_1 (
    .in0(register_1_q), .in1(register_2_q), .in2(register_3_q), .in3(register_4_q), .in4(register_5_q),
    .in5(register_6_q), .in6(register_7_q), .in7(register_8_q), .out(out_6), .sel(in_1[2:0]));  // open: en
endmodule

module test (
  output [7:0] out_1,
  output [7:0] out_2,
  output [31:0] out_3,
  output [7:0] out_4
);

  wire clock_1_out, clock_2_out;
  wire [7:0] screendecoder_1_out_3, screendecoder_1_out_4, screendecoder_1_out_5, screendecoder_1_out_6,
       screendecoder_1_out_7, screendecoder_1_out_8, screendecoder_1_out_9, screendecoder_1_out_10;

  Decoder #(.select(3)) decoder_1 (.sel(3'b101));  // open: out0, out1, out2, out3, out4, out5, out6, out7, en
  Clock clock_1 (.out(clock_1_out));
  RegistetGroup registetgroup_1 (
    .in_1(5'b00001), .in_2(8'h22), .in_3(5'b00001), .in_4(1'b1), .in_5(clock_1_out), .out_6(out_4));
  ALU alu_1 (.in_1(8'h22), .in_2(8'h11), .out_4(out_1), .in_3(4'b1010));
  Clock clock_2 (.out(clock_2_out));
  ScreenDecoder screendecoder_1 (
    .out_3(screendecoder_1_out_3), .out_4(screendecoder_1_out_4), .out_5(screendecoder_1_out_5),
    .out_6(screendecoder_1_out_6), .out_7(screendecoder_1_out_7), .out_8(screendecoder_1_out_8),
    .out_9(screendecoder_1_out_9), .out_10(screendecoder_1_out_10), .in_2(8'h4), .in_1(8'h2));
  PC pc_1 (.in_3(clock_2_out), .out_4(out_2), .in_1(1'b0), .in_2({8{1'b0}}));
  DotMatrix #(.matrixcols(8), .matrixrows(8)) dotmatrix_1 (
    .col0(screendecoder_1_out_3), .col1(screendecoder_1_out_4), .col2(screendecoder_1_out_5),
    .col3(screendecoder_1_out_6), .col4(screendecoder_1_out_7), .col5(screendecoder_1_out_8),
    .col6(screendecoder_1_out_9), .col7(screendecoder_1_out_10));
  ROM #(.dataWidth(32)) rom_1 (.addr(out_2), .data(out_3));  // open: sel

  // Notes on the sheet:
  //   contents of rom_1 (hex, n*v repeats v):
  //   0 22222222 f3333333 4fffffff 55555555 77777777 8888888 99999999
endmodule

module RegisterGroupV2 (
  input  [4:0] in_1,
  input  [4:0] in_2,
  input  [7:0] in_3,
  input  [4:0] in_4,
  input  in_5,
  input  in_6,
  output [7:0] out_7,
  output [7:0] out_8,
  output [7:0] out_9,
  output [7:0] out_10,
  output [7:0] out_11
);

  wire and_1_out, and_2_out, and_3_out, and_4_out, and_5_out, and_6_out, and_7_out, decoder_1_out0,
       decoder_1_out1, decoder_1_out2, decoder_1_out3, decoder_1_out4, decoder_1_out5, decoder_1_out6,
       decoder_1_out7;
  wire [7:0] register_1_q, register_2_q, register_3_q, register_4_q, register_8_q;

  Decoder #(.select(3)) decoder_1 (
    .out0(decoder_1_out0), .out1(decoder_1_out1), .out2(decoder_1_out2), .out3(decoder_1_out3),
    .out4(decoder_1_out4), .out5(decoder_1_out5), .out6(decoder_1_out6), .out7(decoder_1_out7),
    .sel(in_4[2:0]));  // open: en
  and and_1 (and_1_out, in_5, decoder_1_out0);
  and and_2 (and_2_out, in_5, decoder_1_out1);
  and and_3 (and_3_out, in_5, decoder_1_out2);
  and and_4 (and_4_out, in_5, decoder_1_out3);
  and and_5 (and_5_out, in_5, decoder_1_out4);
  and and_6 (and_6_out, in_5, decoder_1_out5);
  and and_7 (and_7_out, in_5, decoder_1_out6);
  // AND_Gate and_8 has open pins: in0=in_5, in1=decoder_1_out7, out=open
  Register register_1 (.D(in_3), .en(and_1_out), .Q(register_1_q), .clk(in_6));  // open: clr
  Register register_2 (.D(in_3), .en(and_2_out), .Q(register_2_q), .clk(in_6));  // open: clr
  Register register_3 (.D(in_3), .en(and_3_out), .Q(register_3_q), .clk(in_6));  // open: clr
  Register register_4 (.D(in_3), .en(and_4_out), .Q(register_4_q), .clk(in_6));  // open: clr
  Register register_5 (.D(in_3), .en(and_5_out), .Q(out_9), .clk(in_6));  // open: clr
  Register register_6 (.D(in_3), .en(and_6_out), .Q(out_10), .clk(in_6));  // open: clr
  Register register_7 (.D(in_3), .en(and_7_out), .Q(out_11), .clk(in_6));  // open: clr
  Register register_8 (.Q(register_8_q), .clr(1'b1));  // open: D, en, clk
  Multiplexer #(.select(3), .width(8)) multiplexer_1 (
    .in0(register_1_q), .in1(register_2_q), .in2(register_3_q), .in3(register_4_q), .in4(out_9),
    .in5(out_10), .in6(out_11), .in7(register_8_q), .out(out_7), .sel(in_1[2:0]));  // open: en
  Multiplexer #(.select(3), .width(8)) multiplexer_2 (
    .in0(register_1_q), .in1(register_2_q), .in2(register_3_q), .in3(register_4_q), .in4(out_9),
    .in5(out_10), .in6(out_11), .in7(register_8_q), .out(out_8), .sel(in_2[2:0]));  // open: en
endmodule

module PC (
  input  in_1,
  input  [7:0] in_2,
  input  in_3,
  output [7:0] out_4
);

  wire [7:0] adder_1_out, multiplexer_1_out;

  Adder adder_1 (.a(out_4), .b(8'h1), .out(adder_1_out));  // open: cin, cout
  Multiplexer #(.width(8)) multiplexer_1 (
    .in0(adder_1_out), .in1(in_2), .out(multiplexer_1_out), .sel(in_1));  // open: en
  Register register_1 (.D(multiplexer_1_out), .en(1'b1), .Q(out_4), .clk(in_3));  // open: clr
endmodule

module ScreenDecoder (
  input  [7:0] in_1,
  input  [7:0] in_2,
  output [7:0] out_3,
  output [7:0] out_4,
  output [7:0] out_5,
  output [7:0] out_6,
  output [7:0] out_7,
  output [7:0] out_8,
  output [7:0] out_9,
  output [7:0] out_10
);

  wire decoder_1_out0, decoder_1_out1, decoder_1_out2, decoder_1_out3, decoder_1_out4, decoder_1_out5,
       decoder_1_out6, decoder_1_out7, decoder_2_out0, decoder_2_out1, decoder_2_out2, decoder_2_out3,
       decoder_2_out4, decoder_2_out5, decoder_2_out6, decoder_2_out7;
  wire [2:0] bit_extender_1_out, bit_extender_2_out;

  Decoder #(.select(3)) decoder_1 (
    .out0(decoder_1_out0), .out1(decoder_1_out1), .out2(decoder_1_out2), .out3(decoder_1_out3),
    .out4(decoder_1_out4), .out5(decoder_1_out5), .out6(decoder_1_out6), .out7(decoder_1_out7),
    .sel(bit_extender_1_out));  // open: en
  Bit_Extender #(.out_width(3)) bit_extender_1 (.in(in_2), .out(bit_extender_1_out));
  and and_1 (out_3[0], decoder_2_out0, decoder_1_out0);
  and and_2 (out_3[1], decoder_2_out0, decoder_1_out1);
  and and_3 (out_3[2], decoder_2_out0, decoder_1_out2);
  and and_4 (out_3[3], decoder_2_out0, decoder_1_out3);
  and and_5 (out_3[4], decoder_2_out0, decoder_1_out4);
  and and_6 (out_3[5], decoder_2_out0, decoder_1_out5);
  and and_7 (out_3[6], decoder_2_out0, decoder_1_out6);
  and and_8 (out_3[7], decoder_2_out0, decoder_1_out7);
  and and_9 (out_4[0], decoder_2_out1, decoder_1_out0);
  and and_10 (out_4[1], decoder_2_out1, decoder_1_out1);
  and and_11 (out_4[2], decoder_2_out1, decoder_1_out2);
  and and_12 (out_4[3], decoder_2_out1, decoder_1_out3);
  and and_13 (out_4[4], decoder_2_out1, decoder_1_out4);
  and and_14 (out_4[5], decoder_2_out1, decoder_1_out5);
  and and_15 (out_4[6], decoder_2_out1, decoder_1_out6);
  and and_16 (out_4[7], decoder_2_out1, decoder_1_out7);
  and and_17 (out_5[0], decoder_2_out2, decoder_1_out0);
  and and_18 (out_5[1], decoder_2_out2, decoder_1_out1);
  and and_19 (out_5[2], decoder_2_out2, decoder_1_out2);
  and and_20 (out_5[3], decoder_2_out2, decoder_1_out3);
  and and_21 (out_5[4], decoder_2_out2, decoder_1_out4);
  and and_22 (out_5[5], decoder_2_out2, decoder_1_out5);
  and and_23 (out_5[6], decoder_2_out2, decoder_1_out6);
  and and_24 (out_5[7], decoder_2_out2, decoder_1_out7);
  Decoder #(.select(3)) decoder_2 (
    .out0(decoder_2_out0), .out1(decoder_2_out1), .out2(decoder_2_out2), .out3(decoder_2_out3),
    .out4(decoder_2_out4), .out5(decoder_2_out5), .out6(decoder_2_out6), .out7(decoder_2_out7),
    .sel(bit_extender_2_out));  // open: en
  Bit_Extender #(.out_width(3)) bit_extender_2 (.in(in_1), .out(bit_extender_2_out));
  and and_25 (out_6[0], decoder_2_out3, decoder_1_out0);
  and and_26 (out_6[1], decoder_2_out3, decoder_1_out1);
  and and_27 (out_6[2], decoder_2_out3, decoder_1_out2);
  and and_28 (out_6[3], decoder_2_out3, decoder_1_out3);
  and and_29 (out_6[4], decoder_2_out3, decoder_1_out4);
  and and_30 (out_6[5], decoder_2_out3, decoder_1_out5);
  and and_31 (out_6[6], decoder_2_out3, decoder_1_out6);
  and and_32 (out_6[7], decoder_2_out3, decoder_1_out7);
  and and_33 (out_7[0], decoder_2_out4, decoder_1_out0);
  and and_34 (out_7[1], decoder_2_out4, decoder_1_out1);
  and and_35 (out_7[2], decoder_2_out4, decoder_1_out2);
  and and_36 (out_7[3], decoder_2_out4, decoder_1_out3);
  and and_37 (out_7[4], decoder_2_out4, decoder_1_out4);
  and and_38 (out_7[5], decoder_2_out4, decoder_1_out5);
  and and_39 (out_7[6], decoder_2_out4, decoder_1_out6);
  and and_40 (out_7[7], decoder_2_out4, decoder_1_out7);
  and and_41 (out_8[0], decoder_2_out5, decoder_1_out0);
  and and_42 (out_8[1], decoder_2_out5, decoder_1_out1);
  and and_43 (out_8[2], decoder_2_out5, decoder_1_out2);
  and and_44 (out_8[3], decoder_2_out5, decoder_1_out3);
  and and_45 (out_8[4], decoder_2_out5, decoder_1_out4);
  and and_46 (out_8[5], decoder_2_out5, decoder_1_out5);
  and and_47 (out_8[6], decoder_2_out5, decoder_1_out6);
  and and_48 (out_8[7], decoder_2_out5, decoder_1_out7);
  and and_49 (out_9[0], decoder_2_out6, decoder_1_out0);
  and and_50 (out_9[1], decoder_2_out6, decoder_1_out1);
  and and_51 (out_9[2], decoder_2_out6, decoder_1_out2);
  and and_52 (out_9[3], decoder_2_out6, decoder_1_out3);
  and and_53 (out_9[4], decoder_2_out6, decoder_1_out4);
  and and_54 (out_9[5], decoder_2_out6, decoder_1_out5);
  and and_55 (out_9[6], decoder_2_out6, decoder_1_out6);
  and and_56 (out_9[7], decoder_2_out6, decoder_1_out7);
  and and_57 (out_10[0], decoder_2_out7, decoder_1_out0);
  and and_58 (out_10[1], decoder_2_out7, decoder_1_out1);
  and and_59 (out_10[2], decoder_2_out7, decoder_1_out2);
  and and_60 (out_10[3], decoder_2_out7, decoder_1_out3);
  and and_61 (out_10[4], decoder_2_out7, decoder_1_out4);
  and and_62 (out_10[5], decoder_2_out7, decoder_1_out5);
  and and_63 (out_10[6], decoder_2_out7, decoder_1_out6);
  and and_64 (out_10[7], decoder_2_out7, decoder_1_out7);
endmodule
